# Fritzing sketch Wifi Modem Schematic (saved by Fritzing 0.9.2b)
perfboards: 1

parts:
  U1 = NodeMCU V3.0

nets:
  N1: U1.GND#6, U1.GND#13, U1.GND#16, U1.GND#33

custom parts:
  NodeMCU V3.0: ESP8266 based NodeMCU
